# Fritzing sketch Untitled Sketch 2 (saved by Fritzing 0.9.3b)
circuit board: 11.2751cm x 8.30678cm

parts:
  DHT1 = DHT22 Humidity and Temperature Sensor
  Componente1 = Adafruit ADS1115 16Bit I2C ADC [part_number="Adafruit #1085"]
  Componente2 = Adafruit ADS1115 16Bit I2C ADC [part_number="Adafruit #1085"]
  Componente3 = Adafruit ADS1115 16Bit I2C ADC [part_number="Adafruit #1085"]
  Componente4 = RFM9xW
  ANT1 = Antenna
  Componente5 = Arduino Pro Mini (5V)
  VCC1 = 4 x AAA Battery Mount
  U3 = SWITCH_SPDT [package=kps-1290]
  M1 = Alphasense_ISB [package=THT]
  M2 = Alphasense_ISB [package=THT]
  M3 = Alphasense_ISB [package=THT]

nets:
  VDD: DHT1.VDD, Componente1.VDD, Componente2.ADDR, Componente2.VDD, Componente3.VDD, Componente4.VCC, Componente5.VCC, M1.VIN+, M2.VIN+, M3.VIN+
  N1: DHT1.DATA, Componente5.D7
  GND: DHT1.GND, Componente1.ADDR, Componente1.GND, Componente2.GND, Componente3.GND, Componente4.GND#7, Componente5.GND, VCC1.-, M1.OP2-, M1.OP1-, M1.VIN-, M2.OP2-, M2.OP1-, M2.VIN-, M3.OP2-, M3.OP1-, M3.VIN-
  N2: Componente1.AIN3, M1.OP2+
  N3: Componente1.AIN1, M1.OP1+
  N4: Componente1.SDA, Componente2.SDA, Componente3.SDA, Componente5.A4
  N5: Componente1.SCL, Componente2.SCL, Componente3.ADDR, Componente3.SCL, Componente5.A5
  N6: Componente2.AIN3, M2.OP2+
  N7: Componente2.AIN1, M2.OP1+
  N8: Componente3.AIN3, M3.OP2+
  N9: Componente3.AIN1, M3.OP1+
  N10: Componente4.MOSI, Componente5.MOSI
  N11: Componente4.SCK, Componente5.SCK
  N12: Componente4.NSS, Componente5.D6
  N13: Componente4.RESET, Componente5.D5
  N14: Componente4.ANT, ANT1.antenna_lead
  N15: Componente4.DIO0, Componente5.D2
  N16: Componente4.DIO1, Componente5.D3
  N17: Componente4.DIO2, Componente5.D4
  N18: VCC1.+, U3.O

custom parts:
  Adafruit ADS1115 16Bit I2C ADC: For microcontrollers without an analog-to-digital converter or when you want a higher-precision ADC, the ADS1115 provides 16-bit precision at 860 samples/second over I2C. The chip can be configured as 4 single-ended input channels, or two differential channels. As a nice bonus, it even includes a programmable gain amplifier, up to x16, to help boost up smaller single/differential signals to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
  RFM9xW: RFM9xW Module connector
  Alphasense_ISB: Alphasense Individual Sensor Board for gas sensors
