# Fritzing sketch projeto (saved by Fritzing 0.9.3b)
circuit board: 8.46667cm x 5.64444cm
breadboards: 1

parts:
  Componente1 = Arduino Pro Mini (3.3V)
  DHT1 = DHT22 Humidity and Temperature Sensor
  Componente3 = RFM9xW
  U2 = SWITCH_SPDT [package=kps-1290]
  U3 = LIPO-110mAh [package=lipo-110]
  ANT1 = Antenna
  R1 = Resistor [tolerance=±5% resistance=1M package=THT]
  R2 = Resistor [tolerance=±5% resistance=330k package=THT]

nets:
  N1: Componente1.RAW, U2.P, R1.Pin_0
  N2: Componente1.GND, Componente3.GND#7, U3.-, R2.Pin_1
  VCC: Componente1.VCC, DHT1.VDD, Componente3.VCC
  N3: Componente1.A0, R1.Pin_1, R2.Pin_0
  N4: Componente1.SCK, Componente3.SCK
  N5: Componente1.MOSI, Componente3.MOSI
  N6: Componente1.D7, DHT1.DATA
  N7: Componente1.D6, Componente3.NSS
  N8: Componente1.D5, Componente3.RESET
  N9: Componente1.D4, Componente3.DIO2
  N10: Componente1.D3, Componente3.DIO1
  N11: Componente1.D2, Componente3.DIO0
  N12: Componente3.ANT, ANT1.antenna_lead
  N13: U2.O, U3.+

custom parts:
  RFM9xW: RFM9xW Module connector
