# Fritzing sketch projeto (saved by Fritzing 0.9.3b)
perfboards: 1

parts:
  Componente1 = Arduino Pro Mini (3.3V)
  MPX4250AP1 = MPX4250AP pressure sensor [part_number=MPX]
  DHT1 = DHT22 Humidity and Temperature Sensor
  Componente3 = RFM9xW
  U2 = SWITCH_SPDT [package=kps-1290]
  U3 = LIPO-110mAh [package=lipo-110]
  Componente4 = MQ-7 breakout
  ANT1 = Antenna
  LED1 = smd LED [color="Orange (620nm)" package="0603 [SMD]"]

nets:
  N1: Componente1.RAW, U2.O, U2.P, U3.+
  N2: Componente1.GND, U3.-
  VCC: Componente1.VCC, Componente3.VCC
  N3: Componente1.A1, Componente4.AO
  N4: Componente1.A0, MPX4250AP1.V_out
  N5: Componente1.SCK, Componente3.SCK
  N6: Componente1.MOSI, Componente3.MOSI
  N7: Componente1.D8, LED1.anode
  N8: Componente1.D7, DHT1.DATA
  N9: Componente1.D6, Componente3.NSS
  N10: Componente1.D5, Componente3.RESET
  N11: Componente1.D4, Componente3.DIO2
  N12: Componente1.D3, Componente3.DIO1
  N13: Componente1.D2, Componente3.DIO0
  N14: Componente3.ANT, ANT1.antenna_lead
  N15: Componente3.GND#9, LED1.cathode

custom parts:
  RFM9xW: RFM9xW Module connector
  MQ-7 breakout: SKU: 101282
